# Fritzing sketch drifterWiringV1 5 (saved by Fritzing 0.9.9b)
stripboards: 2

parts:
  Part2 = Adafruit HUZZAH32 ESP32 Feather [part_number="Adafruit #3405"]
  Part3 = Adafruit Adalogger FeatherWing [part_number="Adafruit #2922"]
  A1 = Honeywell 26pcxxh6d [package=THT]
  DS1 = DS18B20 1-Wire Temperature Sensor [part_number=DS18B20]
  DS2 = DS18B20 1-Wire Temperature Sensor [part_number=DS18B20]
  DS3 = DS18B20 1-Wire Temperature Sensor [part_number=DS18B20]
  R1 = Resistor [tolerance=±5% resistance=4.7k package="0402 [SMD]"]
  R2 = Resistor [tolerance=±5% resistance=4.7k package="0402 [SMD]"]
  R3 = Resistor [tolerance=±5% resistance=4.7k package="0402 [SMD]"]
  A2 = Pololu DV24V50F5
  R4 = Temperature Sensor (Thermistor) [thermistor_type=NTC package=THT]
  R5 = Resistor [tolerance=±5% resistance=4.7k package="1206 [SMD]"]
  Part4 = Adafruit RFM9x LoRa Radio [part_number="Adafruit #3072 and #3073"]
  Part5 = Adafruit Ultimate GPS v3 [part_number="Adafruit #746"]  # not connected
  ANT1 = Antenna  # not connected
  ANT2 = Antenna  # not connected
  Part6 = Adafruit HUZZAH32 ESP32 Feather [part_number="Adafruit #3405"]
  Part7 = Adafruit Adalogger FeatherWing [part_number="Adafruit #2922"]  # not connected
  DHT1 = DHT22 Humidity and Temperature Sensor  # not connected
  Part8 = 9-DOF Absolute Orientation IMU Fusion Breakout - BNO055  # not connected
  A3 = Honeywell 26pcxxh6d [package=THT]  # not connected
  Part9 = Adafruit TSL2591 High Dynamic Range Digital Light Sensor [part_number="Adafruit #1980"]  # not connected
  Part10 = Analog Digital MUX Breakout  # not connected
  Part11 = Adafruit RFM9x LoRa Radio [part_number="Adafruit #3072 and #3073"]  # not connected
  R6 = Resistor [tolerance=±5% resistance=10k package="1206 [SMD]"]  # not connected
  Part12 = Adafruit BMP180  # not connected
  Part13 = INA219 High Side DC Current Sensor Breakout [part_number=904]  # not connected

nets:
  N1: Part2.IO16, Part3.RX
  N2: Part2.MISO, Part3.MISO
  N3: Part2.MOSI, Part3.MOSI
  N4: Part2.A2_I34, R5.Pin_1
  N5: Part2.A0_DAC2, A1.pin4
  GND: Part2.GND, A1.pin2, A1.pin3, DS1.GND, DS2.GND, DS3.GND, A2.Pin_3, A2.Pin_4, R4.pin_1
  N6: Part2.VBUS, A1.pin1, A2.Pin_5
  N7: Part2.IO33_A9, DS1.DQ, DS2.DQ, DS3.DQ, R1.Pin_0, R2.Pin_0, R3.Pin_0
  VDD: Part2.IO15_A8, DS1.VDD, DS2.VDD, DS3.VDD, R1.Pin_1, R2.Pin_1, R3.Pin_1
  N8: Part2.IO32_A7, R4.pin_0, R5.Pin_0
  N9: Part2.SCL, Part3.SCL
  N10: Part2.SDA, Part3.SDA
  GND_2: Part4.GND, Part6.GND
  N11: Part4.SCK, Part6.MOSI
  N12: Part4.MISO, Part6.IO16
  N13: Part4.MOSI, Part6.MISO

notes:
  Red - (+) 5v
  Black - (-) 5V
  White - SCL or (+) sig
  Green - SDA or (-) sig
  Blue - MI
  Yellow - MO
  Grey - SCK
  Worth noting that the V regulator can be turned off with EN pin

custom parts:
  Adafruit Adalogger FeatherWing: This is the Adalogger FeatherWing: it adds both a battery-backed Real Time Clock and micro SD card storage to any Feather main board. This FeatherWing will make it real easy to add datalogging to any of our existing Feathers. You get both an I2C real time clock (PCF8523) with 32KHz crystal and battery backup, and a microSD socket that connects to the SPI port pins (+ extra pin for CS). Tested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
  Honeywell 26pcxxh6d: The 26PC Series Miniature Pressure Sensors are small, cost-effective devices intended for use with wet or dry media.
  Pololu DV24V50F5: This small synchronous switching step-down (or buck) regulator takes an input voltage of up to 38 V and efficiently reduces it to 5 V.
  Adafruit RFM9x LoRa Radio: Sending data over long distances is like magic, and now you can be a magician with this range of powerful and easy-to-use radio modules. Sure, sometimes you want to talk to a computer (a good time to use WiFi) or perhaps communicate with a Phone (choose Bluetooth Low Energy!) but what if you want to send data very far? Most WiFi, Bluetooth, Zigbee and other wireless chipsets use 2.4GHz, which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
  Adafruit Ultimate GPS v3: We carry a few different GPS modules here in the Adafruit shop, but none that satisfied our every desire - that's why we designed this little GPS breakout board. We believe this is the Ultimate GPS module, so we named it that. It's got everything you want and more: -165 dBm sensitivity, 10 Hz updates, 66 channels 5V friendly design and only 20mA current draw Breadboard friendly + two mounting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
  9-DOF Absolute Orientation IMU Fusion Breakout - BNO055: A MEMS accelerometer, magnetometer and gyroscope on a single die with a high speed ARM Cortex-M0 based processor to digest all the sensor data, abstract the sensor fusion and real time requirements away, and spit out data you can use in quaternions, Euler angles or vectors.
  Adafruit TSL2591 High Dynamic Range Digital Light Sensor: When the future is dazzlingly-bright, this ultra-high-range luminosity sensor will help you measure it. The TSL2591 luminosity sensor is an advanced digital light sensor, ideal for use in a wide range of light situations. Compared to low cost CdS cells, this sensor is more precise, allowing for exact lux calculations and can be configured for different gain/timing ranges to detect light ranges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
  Adafruit BMP180: This precision sensor from Bosch is the best low-cost sensing solution for measuring barometric pressure and temperature. Because pressure changes with altitude you can also use it as an altimeter! The sensor is soldered onto a PCB with a 3.3V regulator, I2C level shifter and pull-up resistors on the I2C pins. The BMP180 is the next-generation of sensors from Bosch, and replaces the BMP085.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
  INA219 High Side DC Current Sensor Breakout: This breakout board will solve all your power-monitoring problems. Instead of struggling with two multimeters, you can just use the handy INA219B chip on this breakout to both measure both the high side voltage and DC current draw over I2C with 1% precision. Most current-measuring devices such as our current panel meter are only good for low side measuring. That means that unless you want to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
